# Fritzing sketch Vaccine Demo Schematic (saved by Fritzing 0.9.4)
breadboards: 1

parts:
  LED-2A = RGB LED (com. cathode, rgb) [package="5 mm [THT]"]
  LED-3A = RGB LED (com. cathode, rgb) [package="5 mm [THT]"]
  LED-1A = RGB LED (com. cathode, rgb) [package="5 mm [THT]"]
  LED-3B = RGB LED (com. cathode, rgb) [package="5 mm [THT]"]
  LED-1B = RGB LED (com. cathode, rgb) [package="5 mm [THT]"]
  LED-2B = RGB LED (com. cathode, rgb) [package="5 mm [THT]"]
  R1-Red = Resistor [tolerance=±5% resistance=33 package="0805 [SMD]"]
  R1-Green = Resistor [tolerance=±5% resistance=2.4 package="0805 [SMD]"]
  R2-Red = Resistor [tolerance=±5% resistance=33 package="0805 [SMD]"]
  R1-Blue = Resistor [tolerance=±5% resistance=2.4 package="0805 [SMD]"]
  R2-Green = Resistor [tolerance=±5% resistance=2.4 package="0805 [SMD]"]
  R2-Blue = Resistor [tolerance=±5% resistance=2.4 package="0805 [SMD]"]
  R3-Green = Resistor [tolerance=±5% resistance=2.4 package="0805 [SMD]"]
  R3-Red = Resistor [tolerance=±5% resistance=33 package="0805 [SMD]"]
  R3-Blue = Resistor [tolerance=±5% resistance=2.4 package="0805 [SMD]"]
  I2C_Multiplexer = Adafruit TCA9548A
  RGB_Sensor_1 = Adafruit TCS34725 RGB Color Sensor [part_number="Adafruit #1334"]
  RGB_Sensor_2 = Adafruit TCS34725 RGB Color Sensor [part_number="Adafruit #1334"]
  RGB_Sensor_3 = Adafruit TCS34725 RGB Color Sensor [part_number="Adafruit #1334"]
  Raspberry_Pi_4B+ = Raspberry Pi 3 [part_number=RPI-3-V1.2]

nets:
  N1: LED-2A.red_anode, LED-2B.red_anode, R2-Red.Pin_1
  GND: LED-2A.common_cathode, LED-3A.common_cathode, LED-1A.common_cathode, LED-3B.common_cathode, LED-1B.common_cathode, LED-2B.common_cathode, I2C_Multiplexer.GND, RGB_Sensor_1.GND, RGB_Sensor_2.GND, RGB_Sensor_3.GND, Raspberry_Pi_4B+.GND
  N2: LED-2A.green_anode, LED-2B.green_anode, R2-Green.Pin_1
  N3: LED-2A.blue_anode, LED-2B.blue_anode, R2-Blue.Pin_1
  N4: LED-3A.red_anode, LED-3B.red_anode, R3-Red.Pin_1
  N5: LED-3A.green_anode, LED-3B.green_anode, R3-Green.Pin_1
  N6: LED-3A.blue_anode, LED-3B.blue_anode, R3-Blue.Pin_1
  N7: LED-1A.red_anode, LED-1B.red_anode, R1-Red.Pin_1
  N8: LED-1A.green_anode, LED-1B.green_anode, R1-Green.Pin_1
  N9: LED-1A.blue_anode, LED-1B.blue_anode, R1-Blue.Pin_1
  N10: R1-Red.Pin_0, Raspberry_Pi_4B+.GPIO5
  N11: R1-Green.Pin_0, Raspberry_Pi_4B+.GPIO6
  N12: R2-Red.Pin_0, Raspberry_Pi_4B+.GPIO19
  N13: R1-Blue.Pin_0, Raspberry_Pi_4B+.GPIO13
  N14: R2-Green.Pin_0, Raspberry_Pi_4B+.GPIO26
  N15: R2-Blue.Pin_0, Raspberry_Pi_4B+.GPIO12
  N16: R3-Green.Pin_0, Raspberry_Pi_4B+.GPIO20
  N17: R3-Red.Pin_0, Raspberry_Pi_4B+.GPIO16
  N18: R3-Blue.Pin_0, Raspberry_Pi_4B+.GPIO21
  N19: I2C_Multiplexer.3SDA, RGB_Sensor_1.SDA
  N20: I2C_Multiplexer.3SCL, RGB_Sensor_1.SCL
  N21: I2C_Multiplexer.4SDA, RGB_Sensor_2.SDA
  N22: I2C_Multiplexer.4SCL, RGB_Sensor_2.SCL
  N23: I2C_Multiplexer.5SDA, RGB_Sensor_3.SDA
  N24: I2C_Multiplexer.5SCL, RGB_Sensor_3.SCL
  VIN: I2C_Multiplexer.VCC, RGB_Sensor_1.VIN, RGB_Sensor_2.VIN, RGB_Sensor_3.VIN, Raspberry_Pi_4B+.5V
  N25: I2C_Multiplexer.INPUTSDA, Raspberry_Pi_4B+.GPIO2
  N26: I2C_Multiplexer.INPUTSCL, Raspberry_Pi_4B+.GPIO3

custom parts:
  Adafruit TCA9548A: You just found the perfect I2C sensor, and you want to wire up two or three or more of them to your Arduino when you realize "Uh oh, this chip has a fixed I2C address, and from what I know about I2C, you cannot have two devices with the same address on the same SDA/SCL pins!" Are you out of luck? You would be, if you didn't have this ultra-cool TCA9548A 1-to-8 I2C multiplexer! Finally, a way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
  Adafruit TCS34725 RGB Color Sensor: Your electronics can now see in dazzling color with this lovely color light sensor. We found the best color sensor on the market, the TCS34725, which has RGB and Clear light sensing elements. An IR blocking filter, integrated on-chip and localized to the color sensing photodiodes, minimizes the IR spectral component of the incoming light and allows color measurements to be made accurately. The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
